// Logisim project GGweCooked.circ as structural Verilog
module main (
  input  [15:0] in_1,
  input  [15:0] in_2
);

  wire clock, not_1_out, or_1_out, undriven, undriven_2, undriven_3;
  wire [15:0] hackalu_1_out, multiplexer_1_out, multiplexer_2_out, multiplexer_3_out, multiplexer_4_out,
       ram32k_1_data_out, register_1_q, register_2_q;

  Clock #(.highDuration(3), .lowDuration(3)) clock_1 (.out(clock));
  Multiplexer #(.width(16)) multiplexer_1 (.in0({16{1'b0}}), .in1(in_1), .out(multiplexer_1_out), .sel(in_1[15]));
  Multiplexer #(.width(16)) multiplexer_2 (.in0({16{1'b0}}), .in1(in_1), .out(multiplexer_2_out), .sel(not_1_out));
  not not_1 (not_1_out, in_1[15]);
  or or_1 (or_1_out, not_1_out, multiplexer_1_out[5]);
  Multiplexer #(.width(16)) multiplexer_3 (
    .in0({1'b0, multiplexer_2_out[14:0]}), .in1(in_2), .out(multiplexer_3_out), .sel(multiplexer_1_out[5]));
  Multiplexer #(.width(16)) multiplexer_4 (
    .in0(register_1_q), .in1(ram32k_1_data_out), .out(multiplexer_4_out), .sel(multiplexer_1_out[12]));
  Register #(.width(16)) register_1 (.D(multiplexer_3_out), .en(or_1_out), .clk(clock), .Q(register_1_q));  // open: clr
  HackALU hackalu_1 (
    .x(register_2_q), .y(multiplexer_4_out), .zx(multiplexer_1_out[6]), .nx(multiplexer_1_out[7]),
    .zy(multiplexer_1_out[8]), .ny(multiplexer_1_out[9]), .f(multiplexer_1_out[10]), .out(hackalu_1_out));  // open: no, zr, ng
  Register #(.width(16)) register_2 (.D(hackalu_1_out), .en(undriven_2), .clk(clock), .Q(register_2_q));  // open: clr
  // Probe on multiplexer_3_out
  RAM32K ram32k_1 (
    .clk(undriven_3), .write_en(undriven), .addr(register_1_q[14:0]), .data_in(hackalu_1_out),
    .data_out(ram32k_1_data_out));
  // Probe on ram32k_1_data_out

  // Notes on the sheet:
  //   input
  //   D register
  //   A register
endmodule

module ALU (
  input  [15:0] in_1,
  input  zx,
  input  nx,
  input  f,
  input  no,
  input  [15:0] in_6,
  input  zy,
  input  ny,
  output zr,
  output ng,
  output [15:0] \output 
);

  wire [15:0] adder_1_out, and_1_out, multiplexer_1_out, multiplexer_2_out, multiplexer_3_out,
       multiplexer_4_out, multiplexer_5_out, not_1_out, not_2_out, not_3_out;

  Multiplexer #(.width(16)) multiplexer_1 (.in0(in_1), .in1({16{1'b0}}), .out(multiplexer_1_out), .sel(zx));
  Multiplexer #(.width(16)) multiplexer_2 (.in0(in_6), .in1({16{1'b0}}), .out(multiplexer_2_out), .sel(zy));
  assign not_1_out = ~multiplexer_1_out;  // NOT_Gate not_1, 16 bits wide
  assign not_2_out = ~multiplexer_2_out;  // NOT_Gate not_2, 16 bits wide
  Multiplexer #(.width(16)) multiplexer_3 (.in0(multiplexer_1_out), .in1(not_1_out), .out(multiplexer_3_out), .sel(nx));
  Multiplexer #(.width(16)) multiplexer_4 (.in0(multiplexer_2_out), .in1(not_2_out), .out(multiplexer_4_out), .sel(ny));
  Adder #(.width(16)) adder_1 (.a(multiplexer_3_out), .b(multiplexer_4_out), .out(adder_1_out));  // open: cin, cout
  assign and_1_out = multiplexer_3_out & multiplexer_4_out;  // AND_Gate and_1, 16 bits wide
  Multiplexer #(.width(16)) multiplexer_5 (.in0(adder_1_out), .in1(and_1_out), .out(multiplexer_5_out), .sel(f));
  assign not_3_out = ~multiplexer_5_out;  // NOT_Gate not_3, 16 bits wide
  Multiplexer #(.width(16)) multiplexer_6 (
    .in0(multiplexer_5_out), .in1(not_3_out), .out({ng, \output [14:0]}), .sel(no));
  or or_1 (zr, \output [0], \output [1], \output [2], \output [3], \output [4], \output [5], \output [6], \output [7], \output [8], \output [9], \output [10], \output [11], \output [12], \output [13], \output [14], ng);

  assign \output [15] = ng;

  // Notes on the sheet:
  //   X input
  //   Y input
endmodule

module asdasdaw (
  input  [15:0] in_1,
  input  [15:0] in_2
);

  wire clock, clock_1_out, not_1_out, undriven, undriven_2, undriven_3, undriven_4, undriven_5;
  wire [15:0] hackalu_1_out, multiplexer_1_out, multiplexer_2_out, multiplexer_3_out, multiplexer_4_out,
       ram32k_1_data_out, register_1_q, register_2_q;

  Clock #(.highDuration(3), .lowDuration(3)) clock_1 (.out(clock_1_out));
  Multiplexer #(.width(16)) multiplexer_1 (.in0({16{1'b0}}), .in1(in_1), .out(multiplexer_1_out), .sel(in_1[15]));
  Multiplexer #(.width(16)) multiplexer_2 (.in0({16{1'b0}}), .in1(in_1), .out(multiplexer_2_out), .sel(not_1_out));
  not not_1 (not_1_out, in_1[15]);
  // Probe on multiplexer_1_out[5]
  Multiplexer #(.width(16)) multiplexer_3 (
    .in0({1'b0, multiplexer_2_out[14:0]}), .in1(in_2), .out(multiplexer_3_out), .sel(multiplexer_1_out[5]));
  Multiplexer #(.width(16)) multiplexer_4 (
    .in0(register_1_q), .in1(ram32k_1_data_out), .out(multiplexer_4_out), .sel(multiplexer_1_out[12]));
  Register #(.width(16)) register_1 (
    .D(multiplexer_3_out), .en(undriven_2), .clk(undriven_4), .Q(register_1_q));  // open: clr
  HackALU hackalu_1 (
    .x(register_2_q), .y(multiplexer_4_out), .zx(multiplexer_1_out[6]), .nx(multiplexer_1_out[7]),
    .zy(multiplexer_1_out[8]), .ny(multiplexer_1_out[9]), .f(multiplexer_1_out[10]), .out(hackalu_1_out));  // open: no, zr, ng
  Register #(.width(16)) register_2 (.D(hackalu_1_out), .en(undriven_3), .clk(clock), .Q(register_2_q));  // open: clr
  // Probe on multiplexer_3_out
  RAM32K ram32k_1 (
    .clk(undriven_5), .write_en(undriven), .addr(register_1_q[14:0]), .data_in(hackalu_1_out),
    .data_out(ram32k_1_data_out));
  // Probe on ram32k_1_data_out

  // Notes on the sheet:
  //   input
  //   D register
  //   A register
endmodule

// VHDL entity HackALU, as the project stores it:
library IEEE;
use IEEE.STD_LOGIC_1164.ALL;
use IEEE.NUMERIC_STD.ALL;

entity HackALU is
    Port (
        x  : in  STD_LOGIC_VECTOR(15 downto 0);
        y  : in  STD_LOGIC_VECTOR(15 downto 0);
        zx : in  STD_LOGIC;
        nx : in  STD_LOGIC;
        zy : in  STD_LOGIC;
        ny : in  STD_LOGIC;
        f  : in  STD_LOGIC;
        no : in  STD_LOGIC;
        out : out STD_LOGIC_VECTOR(15 downto 0);
        zr  : out STD_LOGIC;
        ng  : out STD_LOGIC
    );
end HackALU;

architecture Behavioral of HackALU is
    signal x1, x2, y1, y2, out1 : STD_LOGIC_VECTOR(15 downto 0);
    signal and_out, add_out    : STD_LOGIC_VECTOR(15 downto 0);
begin

    -- Step 1: Zero the inputs
    x1 <= (others => '0') when zx = '1' else x;
    y1 <= (others => '0') when zy = '1' else y;

    -- Step 2: Negate the inputs
    x2 <= not x1 when nx = '1' else x1;
    y2 <= not y1 when ny = '1' else y1;

    -- Step 3: Compute AND and ADD
    and_out <= x2 and y2;
    add_out <= std_logic_vector(signed(x2) + signed(y2));

    -- Step 4: Function select (f = 1 → add, f = 0 → and)
    out1 <= add_out when f = '1' else and_out;

    -- Step 5: Negate output if no = 1
    out <= not out1 when no = '1' else out1;

    -- Step 6: Zero flag
    zr <= '1' when out = X"0000" else '0';

    -- Step 7: Negative flag (MSB)
    ng <= out(15);

end Behavioral;

// VHDL entity RAM32K, as the project stores it:
library IEEE;
use IEEE.STD_LOGIC_1164.ALL;
use IEEE.NUMERIC_STD.ALL;

entity RAM32K is
    Port (
        clk      : in  std_logic;
        write_en : in  std_logic;
        addr     : in  std_logic_vector(14 downto 0);
        data_in  : in  std_logic_vector(15 downto 0);
        data_out : out std_logic_vector(15 downto 0)
    );
end RAM32K;

architecture Behavioral of RAM32K is
    type ram_type is array (0 to 32767) of std_logic_vector(15 downto 0);
    signal mem : ram_type := (others => (others => '0'));
begin
    process(clk)
    begin
        if rising_edge(clk) then
            if write_en = '1' then
                mem(to_integer(unsigned(addr))) <= data_in;
            end if;
        end if;
    end process;

    data_out <= mem(to_integer(unsigned(addr)));
end Behavioral;

// VHDL entity RAM8K, as the project stores it:
library IEEE;
use IEEE.STD_LOGIC_1164.ALL;
use IEEE.NUMERIC_STD.ALL;

entity RAM8K is
    Port (
        clk      : in  std_logic;
        load     : in  std_logic;
        address  : in  std_logic_vector(12 downto 0);
        in_data  : in  std_logic_vector(15 downto 0);
        out_data : out std_logic_vector(15 downto 0)
    );
end RAM8K;

architecture Behavioral of RAM8K is
    type ram_type is array (0 to 8191) of std_logic_vector(15 downto 0);
    signal mem : ram_type := (others => (others => '0'));
begin
    process(clk)
    begin
        if rising_edge(clk) then
            if load = '1' then
                mem(to_integer(unsigned(address))) <= in_data;
            end if;
        end if;
    end process;

    out_data <= mem(to_integer(unsigned(address)));
end Behavioral;

// VHDL entity Register16, as the project stores it:
library IEEE;
use IEEE.STD_LOGIC_1164.ALL;

entity Register16 is
    Port (
        clk      : in  std_logic;
        load     : in  std_logic;
        in_data  : in  std_logic_vector(15 downto 0);
        out_data : out std_logic_vector(15 downto 0)
    );
end Register16;

architecture Behavioral of Register16 is
    signal state : std_logic_vector(15 downto 0) := (others => '0');
begin
    process(clk)
    begin
        if rising_edge(clk) then
            if load = '1' then
                state <= in_data;
            end if;
        end if;
    end process;

    out_data <= state;
end Behavioral;

// VHDL entity Bit, as the project stores it:
library IEEE;
use IEEE.STD_LOGIC_1164.ALL;

entity Bit is
    Port (
        clk      : in  std_logic;
        load     : in  std_logic;
        in_bit   : in  std_logic;
        out_bit  : out std_logic
    );
end Bit;

architecture Behavioral of Bit is
    signal state : std_logic := '0';
begin
    process(clk)
    begin
        if rising_edge(clk) then
            if load = '1' then
                state <= in_bit;
            end if;
        end if;
    end process;

    out_bit <= state;
end Behavioral;
