// Logisim project final.circ as structural Verilog
module main (
  input  in_1
);

  wire clock, cpufinal_1_writem, undriven;
  wire [13:0] cpufinal_1_addressm, cpufinal_1_pc;
  wire [15:0] cpufinal_1_outm, memory16k_1_out_data, rom16k_1_out_inc;

  Clock clock_1 (.out(clock));
  ROM16K rom16k_1 (.address(cpufinal_1_pc), .out_inc(rom16k_1_out_inc));
  cpufinal cpufinal_1 (
    .inM(memory16k_1_out_data), .instruction(rom16k_1_out_inc), .reset(undriven), .clock(in_1),
    .outM(cpufinal_1_outm), .writeM(cpufinal_1_writem), .addressM(cpufinal_1_addressm), .pc(cpufinal_1_pc));
  Memory16K memory16k_1 (
    .in_data(cpufinal_1_outm), .load(cpufinal_1_writem), .address(cpufinal_1_addressm), .clock(clock),
    .out_data(memory16k_1_out_data));  // open: kbd_in
endmodule

module ALU (
  input  [15:0] in_1,
  input  zx,
  input  nx,
  input  f,
  input  no,
  input  [15:0] in_6,
  input  zy,
  input  ny,
  output zr,
  output ng,
  output [15:0] \output 
);

  wire or_1_out;
  wire [15:0] adder_1_out, and_1_out, multiplexer_1_out, multiplexer_2_out, multiplexer_3_out,
       multiplexer_4_out, multiplexer_5_out, not_1_out, not_2_out, not_3_out;

  Multiplexer #(.width(16)) multiplexer_1 (.in0(in_1), .in1({16{1'b0}}), .out(multiplexer_1_out), .sel(zx));
  Multiplexer #(.width(16)) multiplexer_2 (.in0(in_6), .in1({16{1'b0}}), .out(multiplexer_2_out), .sel(zy));
  assign not_1_out = ~multiplexer_1_out;  // NOT_Gate not_1, 16 bits wide
  assign not_2_out = ~multiplexer_2_out;  // NOT_Gate not_2, 16 bits wide
  Multiplexer #(.width(16)) multiplexer_3 (.in0(multiplexer_1_out), .in1(not_1_out), .out(multiplexer_3_out), .sel(nx));
  Multiplexer #(.width(16)) multiplexer_4 (.in0(multiplexer_2_out), .in1(not_2_out), .out(multiplexer_4_out), .sel(ny));
  Adder #(.width(16)) adder_1 (.a(multiplexer_3_out), .b(multiplexer_4_out), .out(adder_1_out));  // open: cin, cout
  assign and_1_out = multiplexer_3_out & multiplexer_4_out;  // AND_Gate and_1, 16 bits wide
  Multiplexer #(.width(16)) multiplexer_5 (.in0(adder_1_out), .in1(and_1_out), .out(multiplexer_5_out), .sel(f));
  assign not_3_out = ~multiplexer_5_out;  // NOT_Gate not_3, 16 bits wide
  Multiplexer #(.width(16)) multiplexer_6 (
    .in0(multiplexer_5_out), .in1(not_3_out), .out({ng, \output [14:0]}), .sel(no));
  or or_1 (or_1_out, \output [0], \output [1], \output [2], \output [3], \output [4], \output [5], \output [6], \output [7], \output [8], \output [9], \output [10], \output [11], \output [12], \output [13], \output [14], ng);
  not not_4 (zr, or_1_out);

  assign \output [15] = ng;

  // Notes on the sheet:
  //   X input
  //   Y input
endmodule

module CPU (
  input  [15:0] in_1,
  input  [15:0] in_2,
  input  clock,
  input  reset,
  output [15:0] Output,
  output out_6,
  output [13:0] PC,
  output [13:0] out_8
);

  wire and_1_out, and_2_out, and_4_out, and_5_out, and_6_out, and_7_out, and_8_out, not_1_out, not_2_out,
       not_3_out, not_4_out, nx_ng, nx_zr, or_1_out, or_2_out;
  wire [15:0] multiplexer_1_out, multiplexer_2_out, register_1_q;
  wire [15:14] pc_1_out_6, register_2_q;

  not not_1 (not_1_out, in_2[15]);
  // Probe on in_2[15]
  // Probe on not_1_out
  // Probe on nx_zr
  ALU nx (
    .in_1(register_1_q), .zx(in_2[11]), .nx(in_2[10]), .f(in_2[7]), .no(in_2[6]), .in_6(multiplexer_2_out),
    .zy(in_2[9]), .ny(in_2[8]), .zr(nx_zr), .ng(nx_ng), .\output (Output));
  // Probe on nx_ng
  and and_1 (and_1_out, in_2[4], in_2[15]);
  // Probe on and_2_out
  and and_2 (and_2_out, in_2[15], in_2[5]);
  // Probe on Output
  // Probe on not_2_out
  not not_2 (not_2_out, nx_zr);
  // Probe on not_3_out
  not not_3 (not_3_out, nx_ng);
  // Probe on and_1_out
  or or_1 (or_1_out, and_2_out, not_1_out);
  Multiplexer #(.width(16)) multiplexer_1 (
    .in0({in_2[15:4], in_2[15], in_2[2:0]}), .in1(Output), .out(multiplexer_1_out), .sel(and_2_out));
  Register #(.width(16)) register_1 (.D(Output), .en(and_1_out), .clk(clock), .Q(register_1_q));  // open: clr
  // Probe on or_1_out
  // Probe on multiplexer_1_out
  Register #(.width(16)) register_2 (
    .D(multiplexer_1_out), .en(or_1_out), .clk(clock), .Q({register_2_q, PC}));  // open: clr
  // Probe on out_6
  and and_3 (out_6, in_2[15], in_2[15]);
  and and_4 (and_4_out, not_2_out, not_3_out);
  // Probe on multiplexer_2_out
  Multiplexer #(.width(16)) multiplexer_2 (
    .in0({register_2_q, PC}), .in1(in_1), .out(multiplexer_2_out), .sel(in_2[12]));
  // Probe on register_1_q
  // Probe on {register_2_q, PC}
  and and_5 (and_5_out, and_4_out, in_2[2]);
  // Probe on PC
  and and_6 (and_6_out, nx_zr, in_2[1]);
  and and_7 (and_7_out, in_2[15], or_2_out);
  or or_2 (or_2_out, and_5_out, and_6_out, and_8_out);
  not not_4 (not_4_out, and_7_out);
  and and_8 (and_8_out, nx_ng, in_2[0]);
  PC pc_1 (
    .in_1({register_2_q, PC}), .load(and_7_out), .inc(not_4_out), .reset(reset), .in_5(clock),
    .out_6({pc_1_out_6, out_8}));

  assign in_2[3] = in_2[15];

  // Notes on the sheet:
  //   iNPUT
  //   Instructions
  //   f
  //   nf
  //   Cinst
  //   isAinst
  //   Z?
  //   isCInstWriteA
  //   notZ
  //   notN
  //   loadD
  //   ALU output
  //   LoadA
  //   writeM
  //   isPositive
  //   A Regisster
  //   NewAValue
  //   D Regisster
  //   Y
  //   D
  //   A
  //   Jumpone
  //   Maddres
  //   Jumptwo
  //   LoadPc
  //   ShouldJump
  //   Jumpthree
  //   ShouldIncPC
  //   writeM
  //   addresM
endmodule

module PC (
  input  [15:0] in_1,
  input  load,
  input  inc,
  input  reset,
  input  in_5,
  output [15:0] out_6
);

  wire adder_1_cout, or_1_out, or_2_out;
  wire [15:0] adder_1_out, multiplexer_1_out, multiplexer_2_out, multiplexer_3_out;

  Adder #(.width(16)) adder_1 (.a(out_6), .b(16'h1), .out(adder_1_out), .cout(adder_1_cout));  // open: cin
  // Probe on adder_1_cout
  Multiplexer #(.width(16)) multiplexer_1 (.in0(adder_1_out), .in1({16{1'b0}}), .out(multiplexer_1_out), .sel(inc));
  // Probe on adder_1_out
  Multiplexer #(.width(16)) multiplexer_2 (.in0(multiplexer_1_out), .in1(in_1), .out(multiplexer_2_out), .sel(load));
  or or_1 (or_1_out, reset, load);
  Multiplexer #(.width(16)) multiplexer_3 (
    .in0(multiplexer_2_out), .in1({16{1'b0}}), .out(multiplexer_3_out), .sel(reset));
  Register #(.width(16)) register_1 (.D(multiplexer_3_out), .en(or_2_out), .clk(in_5), .Q(out_6));  // open: clr
  or or_2 (or_2_out, or_1_out, inc);

  // Notes on the sheet:
  //   newval
  //   newval
  //   incres
  //   loadres
  //   ora
  //   res reset
  //   changes
endmodule

module Bit (
  input  in_1,
  input  in_2,
  input  in_3,
  output out_4
);

  wire d_ff_1_q, multiplexer_1_out;

  D_Flip_Flop d_ff_1 (.D(multiplexer_1_out), .clk(in_3), .Q(d_ff_1_q));  // open: Qn, preset, reset
  Multiplexer multiplexer_1 (.in0(d_ff_1_q), .in1(in_1), .out(multiplexer_1_out), .sel(in_2));
  or or_1 (out_4, 1'b0, d_ff_1_q);
endmodule

module registerhack (
  input  [15:0] in_1,
  input  in_2,
  input  in_3,
  output [15:0] out_4
);

  LedBar ledbar_1 ();  // open: led0, led1, led2, led3, led4, led5, led6, led7
  Bit bit_1 (.in_1(in_1[0]), .in_2(in_2), .in_3(in_3), .out_4(out_4[0]));
  Bit bit_2 (.in_1(in_1[1]), .in_2(in_2), .in_3(in_3), .out_4(out_4[1]));
  Bit bit_3 (.in_1(in_1[2]), .in_2(in_2), .in_3(in_3), .out_4(out_4[2]));
  Bit bit_4 (.in_1(in_1[3]), .in_2(in_2), .in_3(in_3), .out_4(out_4[3]));
  Bit bit_5 (.in_1(in_1[4]), .in_2(in_2), .in_3(in_3), .out_4(out_4[4]));
  Bit bit_6 (.in_1(in_1[5]), .in_2(in_2), .in_3(in_3), .out_4(out_4[5]));
  Bit bit_7 (.in_1(in_1[6]), .in_2(in_2), .in_3(in_3), .out_4(out_4[6]));
  Bit bit_8 (.in_1(in_1[7]), .in_2(in_2), .in_3(in_3), .out_4(out_4[7]));
  Bit bit_9 (.in_1(in_1[8]), .in_2(in_2), .in_3(in_3), .out_4(out_4[8]));
  Bit bit_10 (.in_1(in_1[9]), .in_2(in_2), .in_3(in_3), .out_4(out_4[9]));
  Bit bit_11 (.in_1(in_1[10]), .in_2(in_2), .in_3(in_3), .out_4(out_4[10]));
  Bit bit_12 (.in_1(in_1[11]), .in_2(in_2), .in_3(in_3), .out_4(out_4[11]));
  Bit bit_13 (.in_1(in_1[12]), .in_2(in_2), .in_3(in_3), .out_4(out_4[12]));
  Bit bit_14 (.in_1(in_1[13]), .in_2(in_2), .in_3(in_3), .out_4(out_4[13]));
  Bit bit_15 (.in_1(in_1[14]), .in_2(in_2), .in_3(in_3), .out_4(out_4[14]));
  Bit bit_16 (.in_1(in_1[15]), .in_2(in_2), .in_3(in_3), .out_4(out_4[15]));
endmodule

module Ram8 (
  input  [15:0] in_1,
  input  in_2,
  input  [2:0] in_3,
  input  in_4,
  output [15:0] out_5
);

  wire [15:0] demultiplexer_1_out0, demultiplexer_1_out1, demultiplexer_1_out2, demultiplexer_1_out3,
       demultiplexer_1_out4, demultiplexer_1_out5, demultiplexer_1_out6, demultiplexer_1_out7,
       registerhack_1_out_4, registerhack_2_out_4, registerhack_3_out_4, registerhack_4_out_4,
       registerhack_5_out_4, registerhack_6_out_4, registerhack_7_out_4, registerhack_8_out_4;

  Demultiplexer #(.select(3), .width(16)) demultiplexer_1 (
    .out0(demultiplexer_1_out0), .out1(demultiplexer_1_out1), .out2(demultiplexer_1_out2),
    .out3(demultiplexer_1_out3), .out4(demultiplexer_1_out4), .out5(demultiplexer_1_out5),
    .out6(demultiplexer_1_out6), .out7(demultiplexer_1_out7), .in(in_1), .sel(in_3));
  // Probe on demultiplexer_1_out0
  registerhack registerhack_1 (.in_1(demultiplexer_1_out0), .in_2(in_2), .in_3(in_4), .out_4(registerhack_1_out_4));
  registerhack registerhack_2 (.in_1(demultiplexer_1_out1), .in_2(in_2), .in_3(in_4), .out_4(registerhack_2_out_4));
  registerhack registerhack_3 (.in_1(demultiplexer_1_out2), .in_2(in_2), .in_3(in_4), .out_4(registerhack_3_out_4));
  registerhack registerhack_4 (.in_1(demultiplexer_1_out3), .in_2(in_2), .in_3(in_4), .out_4(registerhack_4_out_4));
  registerhack registerhack_5 (.in_1(demultiplexer_1_out4), .in_2(in_2), .in_3(in_4), .out_4(registerhack_5_out_4));
  registerhack registerhack_6 (.in_1(demultiplexer_1_out5), .in_2(in_2), .in_3(in_4), .out_4(registerhack_6_out_4));
  registerhack registerhack_7 (.in_1(demultiplexer_1_out6), .in_2(in_2), .in_3(in_4), .out_4(registerhack_7_out_4));
  registerhack registerhack_8 (.in_1(demultiplexer_1_out7), .in_2(in_2), .in_3(in_4), .out_4(registerhack_8_out_4));
  // Probe on registerhack_1_out_4
  mux8way16 mux8way16_1 (
    .in_1(registerhack_1_out_4), .in_2(registerhack_2_out_4), .in_3(registerhack_3_out_4),
    .in_4(registerhack_4_out_4), .in_5(registerhack_5_out_4), .in_6(registerhack_6_out_4),
    .in_7(registerhack_7_out_4), .in_8(registerhack_8_out_4), .in_9(in_3), .out_10(out_5));
endmodule

module mux8way16 (
  input  [15:0] in_1,
  input  [15:0] in_2,
  input  [15:0] in_3,
  input  [15:0] in_4,
  input  [15:0] in_5,
  input  [15:0] in_6,
  input  [15:0] in_7,
  input  [15:0] in_8,
  input  [2:0] in_9,
  output [15:0] out_10
);

  wire [15:0] multiplexer_1_out, multiplexer_2_out, multiplexer_3_out, multiplexer_4_out, multiplexer_5_out,
       multiplexer_6_out;

  Multiplexer #(.width(16)) multiplexer_1 (.in0(in_1), .in1(in_2), .out(multiplexer_1_out), .sel(in_9[0]));
  Multiplexer #(.width(16)) multiplexer_2 (.in0(in_3), .in1(in_4), .out(multiplexer_2_out), .sel(in_9[0]));
  Multiplexer #(.width(16)) multiplexer_3 (.in0(in_5), .in1(in_6), .out(multiplexer_3_out), .sel(in_9[0]));
  Multiplexer #(.width(16)) multiplexer_4 (.in0(in_7), .in1(in_8), .out(multiplexer_4_out), .sel(in_9[0]));
  Multiplexer #(.width(16)) multiplexer_5 (
    .in0(multiplexer_1_out), .in1(multiplexer_2_out), .out(multiplexer_5_out), .sel(in_9[1]));
  Multiplexer #(.width(16)) multiplexer_6 (
    .in0(multiplexer_3_out), .in1(multiplexer_4_out), .out(multiplexer_6_out), .sel(in_9[1]));
  Multiplexer #(.width(16)) multiplexer_7 (
    .in0(multiplexer_5_out), .in1(multiplexer_6_out), .out(out_10), .sel(in_9[2]));
endmodule

// VHDL entity Memory16K, as the project stores it:
library ieee;
use ieee.std_logic_1164.all;
use ieee.numeric_std.all;

entity Memory16K is
    port (
        in_data  : in  std_logic_vector(15 downto 0);
        load     : in  std_logic;
        address  : in  std_logic_vector(13 downto 0); -- Exactly 14 bits
        clock    : in  std_logic;
        kbd_in   : in  std_logic_vector(15 downto 0);
        out_data : out std_logic_vector(15 downto 0)
    );
end entity Memory16K;

architecture Behavioral of Memory16K is
    -- Total array size for 14-bit addressing
    type ram_type is array (0 to 16383) of std_logic_vector(15 downto 0);
    signal mem_array : ram_type := (others => (others => '0'));
    
    signal addr_int : integer;
begin
    addr_int <= to_integer(unsigned(address));

    process(clock)
    begin
        if rising_edge(clock) then
            -- Write logic: Only write if load is 1 and not accessing Keyboard
            if load = '1' and addr_int < 16383 then
                mem_array(addr_int) <= in_data;
            end if;
        end if;
    end process;

    -- Read logic: Memory-mapped I/O check
    process(addr_int, mem_array, kbd_in)
    begin
        if addr_int = 16383 then
            out_data <= kbd_in;    -- Keyboard Input
        else
            out_data <= mem_array(addr_int); -- RAM or Screen
        end if;
    end process;
    
end architecture Behavioral;

// VHDL entity ROM16K, as the project stores it:
library ieee;
use ieee.std_logic_1164.all;
use ieee.numeric_std.all;

entity ROM16K is
    port (
        address : in  std_logic_vector(13 downto 0); -- Exactly 14 bits
        out_inc : out std_logic_vector(15 downto 0)  -- 16-bit instruction
    );
end entity ROM16K;

architecture Behavioral of ROM16K is
    -- 2^14 = 16384
    type rom_type is array (0 to 16383) of std_logic_vector(15 downto 0);
    signal rom_data : rom_type := (others => (others => '0'));
begin
    -- Asynchronous Read
    out_inc <= rom_data(to_integer(unsigned(address)));
end architecture Behavioral;

// VHDL entity cpufinal, as the project stores it:
library ieee;
use ieee.std_logic_1164.all;
use ieee.numeric_std.all;

entity cpufinal is
    port (
        inM         : in  std_logic_vector(15 downto 0); -- Data from Memory
        instruction : in  std_logic_vector(15 downto 0); -- Instruction from ROM
        reset       : in  std_logic;                    -- Reset signal
        clock       : in  std_logic;                    -- Clock signal
        outM        : out std_logic_vector(15 downto 0); -- Data to Memory
        writeM      : out std_logic;                    -- Memory write enable
        addressM    : out std_logic_vector(13 downto 0); -- 14-bit Memory Address
        pc          : out std_logic_vector(13 downto 0)  -- 14-bit ROM Address
    );
end entity cpufinal;

architecture Behavioral of cpufinal is
    -- Internal Registers
    signal reg_A : std_logic_vector(15 downto 0) := (others => '0');
    signal reg_D : std_logic_vector(15 downto 0) := (others => '0');
    signal reg_PC : unsigned(13 downto 0) := (others => '0');

    -- Internal Control Signals
    signal is_C_instr : std_logic;
    signal alu_out    : std_logic_vector(15 downto 0);
    signal zr, ng     : std_logic; -- ALU flags

begin
    -- 1. Decode Instruction Type
    is_C_instr <= instruction(15);
    
    -- 2. ALU Logic (Standard Hack Control Bits)
    process(reg_D, reg_A, inM, instruction, is_C_instr)
        variable x, y, out_v : signed(15 downto 0);
        variable c_bits : std_logic_vector(5 downto 0);
        variable a_bit  : std_logic;
    begin
        x := signed(reg_D);
        a_bit := instruction(12);
        c_bits := instruction(11 downto 6);
        
        -- Select Y: Either A register or Memory input
        if a_bit = '0' then y := signed(reg_A); else y := signed(inM); end if;

        -- ALU Operations based on Hack Specs
        case c_bits is
            when "101010" => out_v := (others => '0'); -- 0
            when "111111" => out_v := to_signed(1, 16); -- 1
            when "111010" => out_v := to_signed(-1, 16);-- -1
            when "001100" => out_v := x;               -- D
            when "110000" => out_v := y;               -- A/M
            when "001101" => out_v := not x;           -- !D
            when "110001" => out_v := not y;           -- !A/M
            when "001111" => out_v := -x;              -- -D
            when "110011" => out_v := -y;              -- -A/M
            when "011111" => out_v := x + 1;           -- D+1
            when "110111" => out_v := y + 1;           -- A/M+1
            when "001110" => out_v := x - 1;           -- D-1
            when "110010" => out_v := y - 1;           -- A/M-1
            when "000010" => out_v := x + y;           -- D+A
            when "010011" => out_v := x - y;           -- D-A
            when "000111" => out_v := y - x;           -- A-D
            when "000000" => out_v := x and y;         -- D&A
            when "010101" => out_v := x or y;          -- D|A
            when others   => out_v := (others => '0');
        end case;

        alu_out <= std_logic_vector(out_v);
        
        -- Flag Logic
        if out_v = 0 then zr <= '1'; else zr <= '0'; end if;
        if out_v < 0 then ng <= '1'; else ng <= '0'; end if;
    end process;

    -- 3. Registers and Program Counter
    process(clock, reset)
        variable load_A, load_D, jump : std_logic;
        variable j_bits : std_logic_vector(2 downto 0);
    begin
        if reset = '1' then
            reg_A <= (others => '0');
            reg_D <= (others => '0');
            reg_PC <= (others => '0');
        elsif rising_edge(clock) then
            -- A Register: Load if A-instr or if C-instr dest bit is set
            load_A := (not is_C_instr) or (is_C_instr and instruction(5));
            if load_A = '1' then
                if is_C_instr = '0' then
                    reg_A <= instruction; -- Store constant
                else
                    reg_A <= alu_out;     -- Store ALU result
                end if;
            end if;

            -- D Register: Load if C-instr and d2 bit is set
            load_D := is_C_instr and instruction(4);
            if load_D = '1' then
                reg_D <= alu_out;
            end if;

            -- PC Jump Logic
            j_bits := instruction(2 downto 0);
            jump := (j_bits(2) and ng) or                       -- JLT
                    (j_bits(1) and zr) or                       -- JEQ
                    (j_bits(0) and (not ng) and (not zr));      -- JGT
            
            -- Full jump check (handles JGE, JLE, JNE, JMP combinations)
            if is_C_instr = '1' and jump = '1' then
                reg_PC <= unsigned(reg_A(13 downto 0)); -- Jump to 14-bit address
            else
                reg_PC <= reg_PC + 1;
            end if;
        end if;
    end process;

    -- 4. Assign Final Outputs
    outM     <= alu_out;
    writeM   <= is_C_instr and instruction(3); -- d3 bit
    addressM <= reg_A(13 downto 0);            -- Truncated to 14 bits
    pc       <= std_logic_vector(reg_PC);      -- 14-bit PC

end architecture Behavioral;
